// Logisim project ex5.circ as structural Verilog: 1 circuit, main circuit main
module main (
  input  T,
  input  in_2,
  output out_3,
  output out_4
);

  _7476__JK_flip_flop_w__clear___preset u_7476_jk_flip_flop_w_clear_preset_1 (
    .J(T), .CLK(in_2), .K(T), .Q(out_3), .Q_2(out_4));  // open: PR, CLR
endmodule
