// Logisim project TTL.circ as structural Verilog: 21 circuits, main circuit 74148 (priority encoder)
module _74148__priority_encoder (
  input  _0,
  input  _1,
  input  _2,
  input  _3,
  input  _4,
  input  _5,
  input  _6,
  input  _7,
  input  EI,
  output EO,
  output GS,
  output A0,
  output A1,
  output A2
);

  wire and_1_out, and_2_out, and_3_out, and_4_out, and_5_out, and_6_out, and_7_out, and_8_out, and_9_out,
       and_10_out, and_11_out, and_12_out, not_1_out;

  not not_1 (not_1_out, EI);
  nand nand_1 (EO, _7, _6, _5, _4, _3, _2, _1, _0, not_1_out);
  and and_1 (and_1_out, ~_1, _2, _4, _6, not_1_out);  // AND_Gate
  and and_2 (and_2_out, ~_3, _4, _6, not_1_out);  // AND_Gate
  and and_3 (and_3_out, ~_5, _6, not_1_out);  // AND_Gate
  and and_4 (and_4_out, ~_7, not_1_out);  // AND_Gate
  and and_5 (and_5_out, ~_2, _4, _5, not_1_out);  // AND_Gate
  and and_6 (and_6_out, ~_3, _4, _5, not_1_out);  // AND_Gate
  and and_7 (and_7_out, ~_6, not_1_out);  // AND_Gate
  and and_8 (and_8_out, ~_7, not_1_out);  // AND_Gate
  and and_9 (and_9_out, ~_4, not_1_out);  // AND_Gate
  and and_10 (and_10_out, ~_5, not_1_out);  // AND_Gate
  and and_11 (and_11_out, ~_6, not_1_out);  // AND_Gate
  and and_12 (and_12_out, ~_7, not_1_out);  // AND_Gate
  nand nand_2 (GS, EO, not_1_out);
  nor nor_1 (A0, and_1_out, and_2_out, and_3_out, and_4_out);
  nor nor_2 (A1, and_5_out, and_6_out, and_7_out, and_8_out);
  nor nor_3 (A2, and_9_out, and_10_out, and_11_out, and_12_out);

  // Notes on the sheet:
  //   _
  //   _
  //   _
  //   _
  //   _
  //   _
  //   _
  //   _
  //   _
  //   _
  //   _
  //   _
  //   _
  //   _
  //   Author: Cristian Vancea
  //   Affiliation: Technical University of Cluj-Napoca
endmodule

module _74151__MUX8_1 (
  input  STROBE,
  input  D0,
  input  D1,
  input  D2,
  input  D3,
  input  D4,
  input  D5,
  input  D6,
  input  D7,
  input  C,
  input  B,
  input  A,
  output Y,
  output W
);

  wire and_1_out, and_2_out, and_3_out, and_4_out, and_5_out, and_6_out, and_7_out, and_8_out, or_1_out;

  and and_1 (and_1_out, D0, ~C, ~B, ~A);  // AND_Gate
  and and_2 (and_2_out, D1, ~C, ~B, A);  // AND_Gate
  and and_3 (and_3_out, D2, ~C, B, ~A);  // AND_Gate
  and and_4 (and_4_out, D3, ~C, B, A);  // AND_Gate
  and and_5 (and_5_out, D4, C, ~B, ~A);  // AND_Gate
  and and_6 (and_6_out, D5, C, ~B, A);  // AND_Gate
  and and_7 (and_7_out, D6, C, B, ~A);  // AND_Gate
  and and_8 (and_8_out, D7, C, B, A);
  or or_1 (or_1_out, and_1_out, and_2_out, and_3_out, and_4_out, and_5_out, and_6_out, and_7_out, and_8_out);
  and and_9 (Y, ~STROBE, or_1_out);  // AND_Gate
  not not_1 (W, Y);

  // Notes on the sheet:
  //   ____
  //   _
  //   Author: Cristian Vancea
  //   Affiliation: Technical University of Cluj-Napoca
endmodule

module _74154__binary_DCD4_16 (
  input  A,
  input  B,
  input  C,
  input  D,
  input  G1,
  input  G2,
  output _0,
  output _1,
  output _2,
  output _3,
  output _4,
  output _5,
  output _6,
  output _7,
  output _8,
  output _9,
  output _10,
  output _11,
  output _12,
  output _13,
  output _14,
  output _15
);

  wire and_1_out, nand_1_out, nand_2_out, nand_3_out, nand_4_out, nand_5_out, nand_6_out, nand_7_out,
       nand_8_out, nand_9_out, nand_10_out, nand_11_out, nand_12_out, nand_13_out, nand_14_out, nand_15_out,
       nand_16_out;

  and and_1 (and_1_out, ~G1, ~G2);  // AND_Gate
  nand nand_1 (nand_1_out, ~D, ~C, ~B, ~A);  // NAND_Gate
  nand nand_2 (nand_2_out, ~D, ~C, ~B, A);  // NAND_Gate
  nand nand_3 (nand_3_out, ~D, ~C, B, ~A);  // NAND_Gate
  nand nand_4 (nand_4_out, ~D, ~C, B, A);  // NAND_Gate
  nand nand_5 (nand_5_out, ~D, C, ~B, ~A);  // NAND_Gate
  nand nand_6 (nand_6_out, ~D, C, ~B, A);  // NAND_Gate
  nand nand_7 (nand_7_out, ~D, C, B, ~A);  // NAND_Gate
  nand nand_8 (nand_8_out, ~D, C, B, A);  // NAND_Gate
  nand nand_9 (nand_9_out, D, ~C, ~B, ~A);  // NAND_Gate
  nand nand_10 (nand_10_out, D, ~C, ~B, A);  // NAND_Gate
  nand nand_11 (nand_11_out, D, ~C, B, ~A);  // NAND_Gate
  nand nand_12 (nand_12_out, D, ~C, B, A);  // NAND_Gate
  nand nand_13 (nand_13_out, D, C, ~B, ~A);  // NAND_Gate
  nand nand_14 (nand_14_out, D, C, ~B, A);  // NAND_Gate
  nand nand_15 (nand_15_out, D, C, B, ~A);  // NAND_Gate
  nand nand_16 (nand_16_out, D, C, B, A);
  and and_2 (_0, and_1_out, nand_1_out);
  and and_3 (_1, and_1_out, nand_2_out);
  and and_4 (_2, and_1_out, nand_3_out);
  and and_5 (_3, and_1_out, nand_4_out);
  and and_6 (_4, and_1_out, nand_5_out);
  and and_7 (_5, and_1_out, nand_6_out);
  and and_8 (_6, and_1_out, nand_7_out);
  and and_9 (_7, and_1_out, nand_8_out);
  and and_10 (_8, and_1_out, nand_9_out);
  and and_11 (_9, and_1_out, nand_10_out);
  and and_12 (_10, and_1_out, nand_11_out);
  and and_13 (_11, and_1_out, nand_12_out);
  and and_14 (_12, and_1_out, nand_13_out);
  and and_15 (_13, and_1_out, nand_14_out);
  and and_16 (_14, and_1_out, nand_15_out);
  and and_17 (_15, and_1_out, nand_16_out);

  // Notes on the sheet:
  //   _
  //   _
  //   _
  //   _
  //   _
  //   _
  //   _
  //   _
  //   _
  //   _
  //   _
  //   _
  //   _
  //   _
  //   _
  //   _
  //   _
  //   _
  //   Author: Cristian Vancea
  //   Affiliation: Technical University of Cluj-Napoca
endmodule

module _74157__MUX2_1_4b (
  input  A1,
  input  B1,
  input  A2,
  input  B2,
  input  A3,
  input  B3,
  input  A4,
  input  B4,
  input  S,
  input  G,
  output Y1,
  output Y2,
  output Y3,
  output Y4
);

  wire and_1_out, and_2_out, and_3_out, and_4_out, and_5_out, and_6_out, and_7_out, and_8_out;

  and and_1 (and_1_out, A1, ~S, ~G);  // AND_Gate
  and and_2 (and_2_out, B1, S, ~G);  // AND_Gate
  and and_3 (and_3_out, A2, ~S, ~G);  // AND_Gate
  and and_4 (and_4_out, B2, S, ~G);  // AND_Gate
  and and_5 (and_5_out, A3, ~S, ~G);  // AND_Gate
  and and_6 (and_6_out, B3, S, ~G);  // AND_Gate
  and and_7 (and_7_out, A4, ~S, ~G);  // AND_Gate
  and and_8 (and_8_out, B4, S, ~G);  // AND_Gate
  or or_1 (Y1, and_1_out, and_2_out);
  or or_2 (Y2, and_3_out, and_4_out);
  or or_3 (Y3, and_5_out, and_6_out);
  or or_4 (Y4, and_7_out, and_8_out);

  // Notes on the sheet:
  //   _
  //   Author: Cristian Vancea
  //   Affiliation: Technical University of Cluj-Napoca
endmodule

module _74162__synch_decade_counter (
  input  SR,
  input  CET,
  input  CEP,
  input  PE,
  input  P0,
  input  P1,
  input  P2,
  input  P3,
  input  CP,
  output TC,
  output Q0,
  output Q1,
  output Q2,
  output Q3
);

  wire and_1_out, and_2_out, and_3_out, and_4_out, and_5_out, and_6_out, and_7_out, and_8_out, and_9_out,
       and_10_out, and_11_out, and_12_out, and_13_out, and_14_out, and_16_out, and_17_out, and_18_out,
       and_19_out, nand_1_out, nand_2_out, nand_3_out, or_1_out, or_2_out, or_3_out, or_4_out;

  and and_1 (and_1_out, CET, CEP);
  and and_2 (and_2_out, CET, CEP, PE);
  and and_3 (and_3_out, P0, ~PE);  // AND_Gate
  and and_4 (and_4_out, P1, ~PE);  // AND_Gate
  and and_5 (and_5_out, P2, ~PE);  // AND_Gate
  and and_6 (and_6_out, P3, ~PE);  // AND_Gate
  nand nand_1 (nand_1_out, and_1_out, Q0);
  nand nand_2 (nand_2_out, and_1_out, Q0, Q1);
  nand nand_3 (nand_3_out, and_1_out, Q0);
  and and_7 (and_7_out, Q0, PE, ~and_1_out);  // AND_Gate
  and and_8 (and_8_out, and_2_out, ~Q0);  // AND_Gate
  and and_9 (and_9_out, Q1, PE, nand_1_out);
  and and_10 (and_10_out, and_2_out, Q0, ~Q1, ~Q3);  // AND_Gate
  and and_11 (and_11_out, Q2, PE, nand_2_out);
  and and_12 (and_12_out, and_2_out, Q0, Q1, ~Q2);  // AND_Gate
  and and_13 (and_13_out, PE, Q3, nand_3_out);
  and and_14 (and_14_out, and_2_out, Q0, Q1, Q2);
  and and_15 (TC, CET, Q0, ~Q1, ~Q2, Q3);  // AND_Gate
  or or_1 (or_1_out, and_7_out, and_3_out, and_8_out);
  or or_2 (or_2_out, and_9_out, and_4_out, and_10_out);
  or or_3 (or_3_out, and_11_out, and_5_out, and_12_out);
  or or_4 (or_4_out, and_13_out, and_6_out, and_14_out);
  D_Flip_Flop d_ff_1 (.clk(CP), .D(and_16_out), .Q(Q0));  // open: Qn, preset, en, reset
  and and_16 (and_16_out, or_1_out, SR);
  D_Flip_Flop d_ff_2 (.clk(CP), .D(and_17_out), .Q(Q1));  // open: Qn, preset, en, reset
  and and_17 (and_17_out, or_2_out, SR);
  D_Flip_Flop d_ff_3 (.clk(CP), .D(and_18_out), .Q(Q2));  // open: Qn, preset, en, reset
  and and_18 (and_18_out, or_3_out, SR);
  D_Flip_Flop d_ff_4 (.clk(CP), .D(and_19_out), .Q(Q3));  // open: Qn, preset, en, reset
  and and_19 (and_19_out, or_4_out, SR);

  // Notes on the sheet:
  //   _
  //   _
  //   Author: Cristian Vancea
  //   Affiliation: Technical University of Cluj-Napoca
endmodule

module _74163__synch_binary_counter (
  input  CLEAR,
  input  LOAD,
  input  ENP,
  input  ENT,
  input  A,
  input  B,
  input  C,
  input  D,
  input  CLK,
  output QA,
  output QB,
  output QC,
  output QD,
  output RCO
);

  wire and_1_out, and_2_out, and_3_out, and_4_out, and_5_out, and_6_out, and_7_out, and_8_out, and_9_out,
       and_10_out, and_11_out, and_12_out, and_13_out, and_14_out, and_15_out, and_16_out, nand_1_out,
       nor_1_out, or_1_out, or_2_out, or_3_out, or_4_out, or_5_out, or_6_out, or_7_out, or_8_out;

  nand nand_1 (nand_1_out, CLEAR, LOAD);
  nor nor_1 (nor_1_out, nand_1_out, ~ENP, ~ENT);  // NOR_Gate
  and and_1 (and_1_out, A, CLEAR, nand_1_out);
  and and_2 (and_2_out, nor_1_out, ~QA);  // AND_Gate
  and and_3 (and_3_out, QA, nor_1_out);
  and and_4 (and_4_out, ~or_1_out, nand_1_out);  // AND_Gate
  and and_5 (and_5_out, B, CLEAR, nand_1_out);
  and and_6 (and_6_out, nor_1_out, QA, ~QB);  // AND_Gate
  and and_7 (and_7_out, QB, QA, nor_1_out);
  and and_8 (and_8_out, ~or_3_out, nand_1_out);  // AND_Gate
  and and_9 (and_9_out, C, CLEAR, nand_1_out);
  and and_10 (and_10_out, nor_1_out, QA, QB, ~QC);  // AND_Gate
  and and_11 (and_11_out, QC, QA, QB, nor_1_out);
  and and_12 (and_12_out, ~or_5_out, nand_1_out);  // AND_Gate
  and and_13 (and_13_out, D, CLEAR, nand_1_out);
  and and_14 (and_14_out, nor_1_out, QA, QB, QC, ~QD);  // AND_Gate
  and and_15 (and_15_out, QD, QA, QB, QC, nor_1_out);
  and and_16 (and_16_out, ~or_7_out, nand_1_out);  // AND_Gate
  or or_1 (or_1_out, and_1_out, and_2_out);
  or or_2 (or_2_out, and_3_out, and_4_out);
  or or_3 (or_3_out, and_5_out, and_6_out);
  or or_4 (or_4_out, and_7_out, and_8_out);
  or or_5 (or_5_out, and_9_out, and_10_out);
  or or_6 (or_6_out, and_11_out, and_12_out);
  or or_7 (or_7_out, and_13_out, and_14_out);
  or or_8 (or_8_out, and_15_out, and_16_out);
  J_K_Flip_Flop j_k_ff_1 (.J(or_1_out), .clk(CLK), .K(or_2_out), .Q(QA));  // open: Qn, preset, en, reset
  J_K_Flip_Flop j_k_ff_2 (.J(or_3_out), .clk(CLK), .K(or_4_out), .Q(QB));  // open: Qn, preset, en, reset
  J_K_Flip_Flop j_k_ff_3 (.J(or_5_out), .clk(CLK), .K(or_6_out), .Q(QC));  // open: Qn, preset, en, reset
  J_K_Flip_Flop j_k_ff_4 (.J(or_7_out), .clk(CLK), .K(or_8_out), .Q(QD));  // open: Qn, preset, en, reset
  nor nor_2 (RCO, ~QA, ~QB, ~QC, ~QD, ~ENT);  // NOR_Gate

  // Notes on the sheet:
  //   ___
  //   ___
  //   Author: Cristian Vancea
  //   Affiliation: Technical University of Cluj-Napoca
endmodule

// B
module _74180__parity_generator_checker (
  input  A,
  input  B,
  input  C,
  input  D,
  input  E,
  input  F,
  input  G,
  input  H,
  input  OI,
  input  EI,
  output E_EVEN,
  output E_ODD
);

  wire and_1_out, and_2_out, and_3_out, and_4_out, not_1_out, xnor_1_out, xnor_2_out, xnor_3_out, xnor_4_out,
       xnor_5_out, xor_1_out, xor_2_out;

  xnor xnor_1 (xnor_1_out, A, B);
  xnor xnor_2 (xnor_2_out, C, D);
  xnor xnor_3 (xnor_3_out, E, F);
  xnor xnor_4 (xnor_4_out, G, H);
  xor xor_1 (xor_1_out, xnor_1_out, xnor_2_out);
  xor xor_2 (xor_2_out, xnor_3_out, xnor_4_out);
  not not_1 (not_1_out, xnor_5_out);
  xnor xnor_5 (xnor_5_out, xor_1_out, xor_2_out);
  and and_1 (and_1_out, xnor_5_out, OI);
  and and_2 (and_2_out, not_1_out, EI);
  and and_3 (and_3_out, EI, xnor_5_out);
  and and_4 (and_4_out, not_1_out, OI);
  and and_5 (E_EVEN, ~and_1_out, ~and_2_out);  // AND_Gate
  and and_6 (E_ODD, ~and_3_out, ~and_4_out);  // AND_Gate

  // Notes on the sheet:
  //   Author: Cristian Vancea
  //   Affiliation: Technical University of Cluj-Napoca
endmodule

module _74181__ALU_4b (
  input  S3,
  input  S2,
  input  S1,
  input  S0,
  input  B3,
  input  A3,
  input  B2,
  input  A2,
  input  B1,
  input  A1,
  input  B0,
  input  A0,
  input  M,
  input  Cn,
  output G,
  output Cn_4,
  output P,
  output F3,
  output F2,
  output A_B,
  output F1,
  output F0
);

  wire and_1_out, and_2_out, and_3_out, and_4_out, and_5_out, and_6_out, and_7_out, and_8_out, and_9_out,
       and_10_out, and_11_out, and_12_out, and_13_out, and_14_out, and_15_out, and_16_out, and_17_out,
       and_18_out, and_19_out, and_20_out, and_21_out, and_22_out, and_23_out, and_24_out, and_25_out,
       and_26_out, and_27_out, and_28_out, and_29_out, and_30_out, and_31_out, and_32_out, and_33_out,
       and_34_out, and_35_out, and_36_out, and_37_out, and_38_out, nand_3_out, nand_4_out, nor_2_out,
       nor_3_out, nor_4_out, nor_5_out, nor_6_out, nor_7_out, nor_8_out, nor_9_out, nor_10_out, nor_11_out,
       nor_12_out, not_1_out, not_2_out, not_3_out, not_4_out, not_5_out, not_6_out, not_7_out, not_8_out,
       not_9_out;

  and and_1 (and_1_out, nor_3_out, nor_3_out);
  nor nor_1 (G, and_1_out, and_3_out, and_2_out, and_5_out);
  and and_2 (and_2_out, nor_2_out, nor_4_out, nor_9_out);
  and and_3 (and_3_out, nor_2_out, nor_6_out);
  and and_4 (and_4_out, B3, S3, A3);
  and and_5 (and_5_out, nor_2_out, nor_4_out, nor_7_out, nor_12_out);
  nor nor_2 (nor_2_out, and_4_out, and_6_out);
  and and_6 (and_6_out, A3, S2, not_1_out);
  not not_1 (not_1_out, B3);
  nand nand_1 (Cn_4, G, nand_3_out);
  nand nand_2 (P, nor_2_out, nor_4_out, nor_7_out, nor_11_out);
  nand nand_3 (nand_3_out, nor_2_out, nor_4_out, nor_7_out, nor_11_out, Cn);
  nor nor_3 (nor_3_out, and_7_out, and_8_out, and_10_out);
  and and_7 (and_7_out, not_1_out, S1);
  and and_8 (and_8_out, S0, B3);
  and and_9 (and_9_out, nor_2_out, not_2_out);
  and and_10 (and_10_out, A3, A3);
  and and_11 (and_11_out, nor_4_out, nor_7_out, nor_11_out, Cn, not_9_out);
  not not_2 (not_2_out, nor_3_out);
  nor nor_4 (nor_4_out, and_12_out, and_13_out);
  and and_12 (and_12_out, B2, S3, A2);
  and and_13 (and_13_out, A2, S2, not_3_out);
  xor xor_1 (F3, and_9_out, nor_5_out);
  nor nor_5 (nor_5_out, and_11_out, and_15_out, and_14_out, and_17_out);
  and and_14 (and_14_out, nor_4_out, nor_9_out, not_9_out);
  and and_15 (and_15_out, nor_4_out, nor_7_out, nor_12_out, not_9_out);
  and and_16 (and_16_out, not_3_out, S1);
  not not_3 (not_3_out, B2);
  and and_17 (and_17_out, nor_6_out, not_9_out);
  nor nor_6 (nor_6_out, and_16_out, and_18_out, and_19_out);
  and and_18 (and_18_out, S0, B2);
  and and_19 (and_19_out, A2, A2);
  and and_20 (and_20_out, nor_4_out, not_4_out);
  and and_21 (and_21_out, nor_7_out, nor_11_out, Cn, not_9_out);
  not not_4 (not_4_out, nor_6_out);
  nor nor_7 (nor_7_out, and_22_out, and_26_out);
  and and_22 (and_22_out, B1, S3, A1);
  xor xor_2 (F2, and_20_out, nor_8_out);
  nor nor_8 (nor_8_out, and_21_out, and_23_out, and_24_out);
  and and_23 (and_23_out, nor_7_out, nor_12_out, not_9_out);
  and and_24 (and_24_out, nor_9_out, not_9_out);
  and and_25 (and_25_out, not_5_out, S1);
  and and_26 (and_26_out, A1, S2, not_5_out);
  not not_5 (not_5_out, B1);
  buf buffer_1 (A_B, and_27_out);
  and and_27 (and_27_out, F3, F2, F1, F0);
  and and_28 (and_28_out, nor_7_out, not_6_out);
  not not_6 (not_6_out, nor_9_out);
  nor nor_9 (nor_9_out, and_25_out, and_29_out, and_30_out);
  and and_29 (and_29_out, S0, B1);
  and and_30 (and_30_out, A1, A1);
  and and_31 (and_31_out, Cn, nor_11_out, not_9_out);
  and and_32 (and_32_out, B0, S3, A0);
  xor xor_3 (F1, and_28_out, nor_10_out);
  nor nor_10 (nor_10_out, and_31_out, and_33_out);
  and and_33 (and_33_out, nor_12_out, not_9_out);
  nor nor_11 (nor_11_out, and_32_out, and_34_out);
  and and_34 (and_34_out, A0, S2, not_7_out);
  not not_7 (not_7_out, B0);
  and and_35 (and_35_out, nor_11_out, not_8_out);
  not not_8 (not_8_out, nor_12_out);
  nor nor_12 (nor_12_out, and_37_out, and_36_out, and_38_out);
  and and_36 (and_36_out, S0, B0);
  and and_37 (and_37_out, not_7_out, S1);
  xor xor_4 (F0, and_35_out, nand_4_out);
  nand nand_4 (nand_4_out, not_9_out, Cn);
  and and_38 (and_38_out, A0, A0);
  not not_9 (not_9_out, M);

  // Notes on the sheet:
  //   __
  //   Author: Cristian Vancea
  //   Affiliation: Technical University of Cluj-Napoca
  //   _
endmodule

module _74192__up_down_decade_counter (
  input  CPD,
  input  CPU,
  input  P0,
  input  P1,
  input  P2,
  input  P3,
  input  PL,
  input  MR,
  output TCD,
  output TCU,
  output Q0,
  output Q1,
  output Q2,
  output Q3
);

  wire and_1_out, and_2_out, and_3_out, and_4_out, and_5_out, and_6_out, and_7_out, multiplexer_1_out,
       multiplexer_2_out, multiplexer_3_out, multiplexer_4_out, multiplexer_5_out, multiplexer_6_out,
       multiplexer_7_out, multiplexer_8_out, nand_1_out, nor_1_out, not_1_out, not_2_out, not_3_out,
       not_4_out, not_5_out, not_6_out, or_1_out, or_2_out, or_3_out;

  not not_1 (not_1_out, CPD);
  not not_2 (not_2_out, CPU);
  nand nand_1 (nand_1_out, ~Q1, ~Q2, ~Q3);  // NAND_Gate
  not not_3 (not_3_out, P0);
  Multiplexer #(.select(2), .enable("false")) multiplexer_1 (
    .in0(P0), .in1(1'b0), .in2(1'b0), .in3(1'b0), .out(multiplexer_1_out), .sel({PL, MR}));
  and and_1 (and_1_out, not_1_out, ~Q0, nand_1_out);  // AND_Gate
  and and_2 (and_2_out, Q0, ~Q3, not_2_out);  // AND_Gate
  not not_4 (not_4_out, P1);
  Multiplexer #(.select(2), .enable("false")) multiplexer_2 (
    .in0(P1), .in1(1'b0), .in2(1'b0), .in3(1'b0), .out(multiplexer_2_out), .sel({PL, MR}));
  and and_3 (and_3_out, not_1_out, ~Q0, ~Q1, nand_1_out);  // AND_Gate
  and and_4 (and_4_out, Q0, Q1, not_2_out);
  not not_5 (not_5_out, P2);
  Multiplexer #(.select(2), .enable("false")) multiplexer_3 (
    .in0(P2), .in1(1'b0), .in2(1'b0), .in3(1'b0), .out(multiplexer_3_out), .sel({PL, MR}));
  and and_5 (and_5_out, not_1_out, ~Q0, ~Q1, ~Q2);  // AND_Gate
  and and_6 (and_6_out, not_2_out, Q0, Q3);
  and and_7 (and_7_out, Q0, Q1, Q2, not_2_out);
  not not_6 (not_6_out, P3);
  Multiplexer #(.select(2), .enable("false")) multiplexer_4 (
    .in0(P3), .in1(1'b0), .in2(1'b0), .in3(1'b0), .out(multiplexer_4_out), .sel({PL, MR}));
  nor nor_1 (nor_1_out, not_1_out, not_2_out);
  Multiplexer #(.select(2), .enable("false")) multiplexer_5 (
    .in0(not_3_out), .in1(1'b1), .in2(1'b0), .in3(1'b1), .out(multiplexer_5_out), .sel({PL, MR}));
  or or_1 (or_1_out, and_1_out, and_2_out);
  Multiplexer #(.select(2), .enable("false")) multiplexer_6 (
    .in0(not_4_out), .in1(1'b1), .in2(1'b0), .in3(1'b1), .out(multiplexer_6_out), .sel({PL, MR}));
  or or_2 (or_2_out, and_3_out, and_4_out);
  Multiplexer #(.select(2), .enable("false")) multiplexer_7 (
    .in0(not_5_out), .in1(1'b1), .in2(1'b0), .in3(1'b1), .out(multiplexer_7_out), .sel({PL, MR}));
  or or_3 (or_3_out, and_5_out, and_6_out, and_7_out);
  Multiplexer #(.select(2), .enable("false")) multiplexer_8 (
    .in0(not_6_out), .in1(1'b1), .in2(1'b0), .in3(1'b1), .out(multiplexer_8_out), .sel({PL, MR}));
  T_Flip_Flop t_ff_1 (
    .clk(nor_1_out), .T(1'b1), .Q(Q0), .preset(multiplexer_1_out), .reset(multiplexer_5_out));  // open: Qn, en
  T_Flip_Flop t_ff_2 (
    .clk(nor_1_out), .T(or_1_out), .Q(Q1), .preset(multiplexer_2_out), .reset(multiplexer_6_out));  // open: Qn, en
  T_Flip_Flop t_ff_3 (
    .clk(nor_1_out), .T(or_2_out), .Q(Q2), .preset(multiplexer_3_out), .reset(multiplexer_7_out));  // open: Qn, en
  T_Flip_Flop t_ff_4 (
    .clk(nor_1_out), .T(or_3_out), .Q(Q3), .preset(multiplexer_4_out), .reset(multiplexer_8_out));  // open: Qn, en
  nand nand_2 (TCD, ~Q0, ~Q1, ~Q2, ~Q3, not_1_out);  // NAND_Gate
  nand nand_3 (TCU, Q0, Q3, not_2_out);

  // Notes on the sheet:
  //   _
  //   Author: Cristian Vancea
  //   Affiliation: Technical University of Cluj-Napoca
  //   __
  //   __
endmodule

module _74193__up_down_binary_counter (
  input  CDn,
  input  CUp,
  input  A,
  input  B,
  input  C,
  input  D,
  input  LOAD,
  input  CLEAR,
  output BORROW,
  output CARRY,
  output QA,
  output QB,
  output QC,
  output QD
);

  wire and_1_out, and_2_out, and_3_out, and_4_out, and_5_out, and_6_out, multiplexer_1_out,
       multiplexer_2_out, multiplexer_3_out, multiplexer_4_out, multiplexer_5_out, multiplexer_6_out,
       multiplexer_7_out, multiplexer_8_out, nor_1_out, not_1_out, not_2_out, not_3_out, not_4_out,
       not_5_out, not_6_out, or_1_out, or_2_out, or_3_out;

  not not_1 (not_1_out, CDn);
  not not_2 (not_2_out, CUp);
  Multiplexer #(.select(2), .enable("false")) multiplexer_1 (
    .in0(A), .in1(1'b0), .in2(1'b0), .in3(1'b0), .out(multiplexer_1_out), .sel({LOAD, CLEAR}));
  and and_1 (and_1_out, not_1_out, ~QA);  // AND_Gate
  and and_2 (and_2_out, QA, not_2_out);
  Multiplexer #(.select(2), .enable("false")) multiplexer_2 (
    .in0(B), .in1(1'b0), .in2(1'b0), .in3(1'b0), .out(multiplexer_2_out), .sel({LOAD, CLEAR}));
  and and_3 (and_3_out, not_1_out, ~QA, ~QB);  // AND_Gate
  and and_4 (and_4_out, QA, QB, not_2_out);
  Multiplexer #(.select(2), .enable("false")) multiplexer_3 (
    .in0(C), .in1(1'b0), .in2(1'b0), .in3(1'b0), .out(multiplexer_3_out), .sel({LOAD, CLEAR}));
  and and_5 (and_5_out, not_1_out, ~QA, ~QB, ~QC);  // AND_Gate
  and and_6 (and_6_out, QA, QB, QC, not_2_out);
  Multiplexer #(.select(2), .enable("false")) multiplexer_4 (
    .in0(D), .in1(1'b0), .in2(1'b0), .in3(1'b0), .out(multiplexer_4_out), .sel({LOAD, CLEAR}));
  nor nor_1 (nor_1_out, not_1_out, not_2_out);
  not not_3 (not_3_out, A);
  or or_1 (or_1_out, and_1_out, and_2_out);
  not not_4 (not_4_out, B);
  or or_2 (or_2_out, and_3_out, and_4_out);
  not not_5 (not_5_out, C);
  or or_3 (or_3_out, and_5_out, and_6_out);
  not not_6 (not_6_out, D);
  Multiplexer #(.select(2), .enable("false")) multiplexer_5 (
    .in0(not_6_out), .in1(1'b1), .in2(1'b0), .in3(1'b1), .out(multiplexer_5_out), .sel({LOAD, CLEAR}));
  Multiplexer #(.select(2), .enable("false")) multiplexer_6 (
    .in0(not_3_out), .in1(1'b1), .in2(1'b0), .in3(1'b1), .out(multiplexer_6_out), .sel({LOAD, CLEAR}));
  Multiplexer #(.select(2), .enable("false")) multiplexer_7 (
    .in0(not_4_out), .in1(1'b1), .in2(1'b0), .in3(1'b1), .out(multiplexer_7_out), .sel({LOAD, CLEAR}));
  Multiplexer #(.select(2), .enable("false")) multiplexer_8 (
    .in0(not_5_out), .in1(1'b1), .in2(1'b0), .in3(1'b1), .out(multiplexer_8_out), .sel({LOAD, CLEAR}));
  nand nand_1 (BORROW, ~QA, ~QB, ~QC, ~QD, not_1_out);  // NAND_Gate
  nand nand_2 (CARRY, QA, QB, QC, QD, not_2_out);
  T_Flip_Flop t_ff_1 (
    .clk(nor_1_out), .T(1'b1), .Q(QA), .preset(multiplexer_1_out), .reset(multiplexer_6_out));  // open: Qn, en
  T_Flip_Flop t_ff_2 (
    .clk(nor_1_out), .T(or_1_out), .Q(QB), .preset(multiplexer_2_out), .reset(multiplexer_7_out));  // open: Qn, en
  T_Flip_Flop t_ff_3 (
    .clk(nor_1_out), .T(or_2_out), .Q(QC), .preset(multiplexer_3_out), .reset(multiplexer_8_out));  // open: Qn, en
  T_Flip_Flop t_ff_4 (
    .clk(nor_1_out), .T(or_3_out), .Q(QD), .preset(multiplexer_4_out), .reset(multiplexer_5_out));  // open: Qn, en

  // Notes on the sheet:
  //   ___
  //   Author: Cristian Vancea
  //   Affiliation: Technical University of Cluj-Napoca
  //   _____
  //   ____
endmodule

module _74194__bidir_universal_shift_reg (
  input  A,
  input  B,
  input  C,
  input  D,
  input  SL,
  input  SR,
  input  S1,
  input  S0,
  input  CLK,
  input  CLEAR,
  output QA,
  output QB,
  output QC,
  output QD
);

  wire multiplexer_1_out, multiplexer_2_out, multiplexer_3_out, multiplexer_4_out, not_1_out;

  not not_1 (not_1_out, CLEAR);
  Multiplexer #(.select(2), .enable("false")) multiplexer_1 (
    .in0(QA), .in1(SR), .in2(QB), .in3(A), .out(multiplexer_1_out), .sel({S1, S0}));
  D_Flip_Flop d_ff_1 (.clk(CLK), .D(multiplexer_1_out), .Q(QA), .reset(not_1_out));  // open: Qn, preset, en
  Multiplexer #(.select(2), .enable("false")) multiplexer_2 (
    .in0(QB), .in1(QA), .in2(QC), .in3(B), .out(multiplexer_2_out), .sel({S1, S0}));
  Multiplexer #(.select(2), .enable("false")) multiplexer_3 (
    .in0(QC), .in1(QB), .in2(QD), .in3(C), .out(multiplexer_3_out), .sel({S1, S0}));
  D_Flip_Flop d_ff_2 (.clk(CLK), .D(multiplexer_2_out), .Q(QB), .reset(not_1_out));  // open: Qn, preset, en
  Multiplexer #(.select(2), .enable("false")) multiplexer_4 (
    .in0(QD), .in1(QC), .in2(SL), .in3(D), .out(multiplexer_4_out), .sel({S1, S0}));
  D_Flip_Flop d_ff_3 (.clk(CLK), .D(multiplexer_3_out), .Q(QC), .reset(not_1_out));  // open: Qn, preset, en
  D_Flip_Flop d_ff_4 (.clk(CLK), .D(multiplexer_4_out), .Q(QD), .reset(not_1_out));  // open: Qn, preset, en

  // Notes on the sheet:
  //   ____
  //   Author: Cristian Vancea
  //   Affiliation: Technical University of Cluj-Napoca
endmodule

module _74283__ADD_4b (
  input  B4,
  input  A4,
  input  B3,
  input  A3,
  input  B2,
  input  A2,
  input  B1,
  input  A1,
  input  C0,
  output C4,
  output S4,
  output S3,
  output S2,
  output S1
);

  wire and_1_out, and_2_out, and_3_out, and_4_out, and_5_out, and_6_out, and_7_out, and_8_out, and_9_out,
       and_10_out, and_11_out, and_12_out, and_13_out, and_14_out, nand_1_out, nand_2_out, nand_3_out,
       nand_4_out, nor_1_out, nor_2_out, nor_3_out, nor_4_out, nor_5_out, nor_6_out, nor_7_out, not_1_out,
       not_2_out;

  nand nand_1 (nand_1_out, B4, A4);
  nor nor_1 (nor_1_out, B4, A4);
  nand nand_2 (nand_2_out, B3, A3);
  nor nor_2 (nor_2_out, B3, A3);
  nand nand_3 (nand_3_out, B2, A2);
  nor nor_3 (nor_3_out, B2, A2);
  nand nand_4 (nand_4_out, B1, A1);
  nor nor_4 (nor_4_out, B1, A1);
  not not_1 (not_1_out, C0);
  and and_1 (and_1_out, nor_2_out, nand_1_out);
  and and_2 (and_2_out, nor_3_out, nand_1_out, nand_2_out);
  and and_3 (and_3_out, nor_4_out, nand_1_out, nand_2_out, nand_3_out);
  and and_4 (and_4_out, nand_1_out, nand_2_out, nand_3_out, nand_4_out, not_1_out);
  and and_5 (and_5_out, nand_1_out, ~nor_1_out);  // AND_Gate
  and and_6 (and_6_out, nor_3_out, nand_2_out);
  and and_7 (and_7_out, nor_4_out, nand_2_out, nand_3_out);
  and and_8 (and_8_out, nand_2_out, nand_3_out, nand_4_out, not_1_out);
  and and_9 (and_9_out, nand_2_out, ~nor_2_out);  // AND_Gate
  and and_10 (and_10_out, nor_4_out, nand_3_out);
  and and_11 (and_11_out, nand_3_out, nand_4_out, not_1_out);
  and and_12 (and_12_out, nand_3_out, ~nor_3_out);  // AND_Gate
  and and_13 (and_13_out, nand_4_out, not_1_out);
  and and_14 (and_14_out, nand_4_out, ~nor_4_out);  // AND_Gate
  not not_2 (not_2_out, not_1_out);
  nor nor_5 (nor_5_out, nor_2_out, and_6_out, and_7_out, and_8_out);
  nor nor_6 (nor_6_out, nor_3_out, and_10_out, and_11_out);
  nor nor_7 (nor_7_out, nor_4_out, and_13_out);
  nor nor_8 (C4, nor_1_out, and_1_out, and_2_out, and_3_out, and_4_out);
  xor xor_1 (S4, and_5_out, nor_5_out);
  xor xor_2 (S3, and_9_out, nor_6_out);
  xor xor_3 (S2, and_12_out, nor_7_out);
  xor xor_4 (S1, and_14_out, not_2_out);

  // Notes on the sheet:
  //   Author: Cristian Vancea
  //   Affiliation: Technical University of Cluj-Napoca
endmodule

module _7442__decimal_DCD (
  input  A,
  input  B,
  input  C,
  input  D,
  output _0,
  output _1,
  output _2,
  output _3,
  output _4,
  output _5,
  output _6,
  output _7,
  output _8,
  output _9
);

  nand nand_1 (_0, ~D, ~C, ~B, ~A);  // NAND_Gate
  nand nand_2 (_1, ~D, ~C, ~B, A);  // NAND_Gate
  nand nand_3 (_2, ~D, ~C, B, ~A);  // NAND_Gate
  nand nand_4 (_3, ~D, ~C, B, A);  // NAND_Gate
  nand nand_5 (_4, ~D, C, ~B, ~A);  // NAND_Gate
  nand nand_6 (_5, ~D, C, ~B, A);  // NAND_Gate
  nand nand_7 (_6, ~D, C, B, ~A);  // NAND_Gate
  nand nand_8 (_7, ~D, C, B, A);  // NAND_Gate
  nand nand_9 (_8, D, ~C, ~B, ~A);  // NAND_Gate
  nand nand_10 (_9, D, ~C, ~B, A);  // NAND_Gate

  // Notes on the sheet:
  //   _
  //   _
  //   _
  //   _
  //   _
  //   _
  //   _
  //   _
  //   _
  //   _
  //   Author: Cristian Vancea
  //   Affiliation: Technical University of Cluj-Napoca
endmodule

module _7447__7SEG_decoder (
  input  A0,
  input  A1,
  input  A2,
  input  A3,
  output a,
  output b,
  output c,
  output d,
  output e,
  output f,
  output g
);

  wire and_1_out, and_2_out, and_3_out, and_4_out, and_5_out, and_6_out, and_7_out, and_8_out, and_9_out,
       and_10_out, and_11_out, and_12_out, and_13_out, and_14_out, and_15_out, and_16_out, and_17_out,
       not_1_out, not_2_out, not_3_out, not_4_out;

  not not_1 (not_1_out, A0);
  not not_2 (not_2_out, A1);
  not not_3 (not_3_out, A2);
  not not_4 (not_4_out, A3);
  and and_1 (and_1_out, A1, A3);
  and and_2 (and_2_out, not_1_out, A2);
  and and_3 (and_3_out, A0, not_2_out, not_3_out, not_4_out);
  and and_4 (and_4_out, A1, A3);
  and and_5 (and_5_out, A0, not_2_out, A2);
  and and_6 (and_6_out, not_1_out, A1, A2);
  and and_7 (and_7_out, A2, A3);
  and and_8 (and_8_out, not_1_out, A1, not_3_out);
  and and_9 (and_9_out, A0, not_2_out, not_3_out);
  and and_10 (and_10_out, not_1_out, not_2_out, A2);
  and and_11 (and_11_out, A0, A1, A2);
  and and_12 (and_12_out, not_2_out, A2);
  and and_13 (and_13_out, A0, A1);
  and and_14 (and_14_out, A1, not_3_out);
  and and_15 (and_15_out, A0, not_3_out, not_4_out);
  and and_16 (and_16_out, A0, A1, A2);
  and and_17 (and_17_out, not_2_out, not_3_out, not_4_out);
  or or_1 (a, and_1_out, and_2_out, and_3_out);
  or or_2 (b, and_4_out, and_5_out, and_6_out);
  or or_3 (c, and_7_out, and_8_out);
  or or_4 (d, and_9_out, and_10_out, and_11_out);
  or or_5 (e, A0, and_12_out);
  or or_6 (f, and_13_out, and_14_out, and_15_out);
  or or_7 (g, and_16_out, and_17_out);

  // Notes on the sheet:
  //   _
  //   _
  //   _
  //   _
  //   _
  //   _
  //   _
  //   Author: Cristian Vancea
  //   Affiliation: Technical University of Cluj-Napoca
endmodule

module _7451__2_x_and_nor (
  input  A1,
  input  B1,
  input  C1,
  input  D1,
  input  E1,
  input  F1,
  input  A2,
  input  B2,
  input  C2,
  input  D2,
  output Y1,
  output Y2
);

  wire and_1_out, and_2_out, and_3_out, and_4_out;

  and and_1 (and_1_out, A1, B1, C1);
  and and_2 (and_2_out, D1, E1, F1);
  and and_3 (and_3_out, A2, B2);
  and and_4 (and_4_out, C2, D2);
  nor nor_1 (Y1, and_1_out, and_2_out);
  nor nor_2 (Y2, and_3_out, and_4_out);

  // Notes on the sheet:
  //   Author: Cristian Vancea
  //   Affiliation: Technical University of Cluj-Napoca
endmodule

module _7473__JK_flip_flop_w__clear (
  input  J,
  input  CLK,
  input  K,
  input  CLR,
  output Q,
  output Q_2
);

  wire not_1_out, not_2_out;

  not not_1 (not_1_out, CLK);
  J_K_Flip_Flop j_k_ff_1 (.J(J), .clk(not_1_out), .K(K), .Q(Q), .Qn(Q_2), .reset(not_2_out));  // open: preset, en
  not not_2 (not_2_out, CLR);

  // Notes on the sheet:
  //   __
  //   _
  //   Author: Cristian Vancea
  //   Affiliation: Technical University of Cluj-Napoca
endmodule

module _7474__D_flip_flop_w__clear___preset (
  input  PR,
  input  CLK,
  input  D,
  input  CLR,
  output Q,
  output Q_2
);

  wire not_1_out, not_2_out;

  not not_1 (not_1_out, PR);
  D_Flip_Flop d_ff_1 (.clk(CLK), .D(D), .Q(Q), .Qn(Q_2), .preset(not_1_out), .reset(not_2_out));  // open: en
  not not_2 (not_2_out, CLR);

  // Notes on the sheet:
  //   _
  //   __
  //   _
  //   Author: Cristian Vancea
  //   Affiliation: Technical University of Cluj-Napoca
endmodule

module _7476__JK_flip_flop_w__clear___preset (
  input  PR,
  input  J,
  input  CLK,
  input  K,
  input  CLR,
  output Q,
  output Q_2
);

  wire not_1_out, not_2_out, not_3_out;

  not not_1 (not_1_out, PR);
  not not_2 (not_2_out, CLK);
  J_K_Flip_Flop j_k_ff_1 (
    .J(J), .clk(not_2_out), .K(K), .Q(Q), .Qn(Q_2), .preset(not_1_out), .reset(not_3_out));  // open: en
  not not_3 (not_3_out, CLR);

  // Notes on the sheet:
  //   _
  //   __
  //   _
  //   Author: Cristian Vancea
  //   Affiliation: Technical University of Cluj-Napoca
endmodule

module _7490__asynch_decade_counter (
  input  R9_1,
  input  R9_2,
  input  A,
  input  B,
  input  R0_1,
  input  R0_2,
  output QA,
  output QB,
  output QC,
  output QD
);

  wire and_1_out, n7476_jk_flip_flop_w_clear_preset_2_q_2, nand_1_out, nand_2_out, nor_1_out, nor_2_out;

  nand nand_1 (nand_1_out, R9_1, R9_2);
  nand nand_2 (nand_2_out, R0_1, nand_1_out, R0_2);
  and and_1 (and_1_out, QC, QB);
  _7476__JK_flip_flop_w__clear___preset u_7476_jk_flip_flop_w_clear_preset_1 (
    .J(1'b1), .CLK(A), .K(1'b1), .Q(QA), .PR(nand_1_out), .CLR(nand_2_out));  // open: Q_2
  _7473__JK_flip_flop_w__clear u_7473_jk_flip_flop_w_clear_1 (
    .Q(QB), .CLR(nor_1_out), .J(n7476_jk_flip_flop_w_clear_preset_2_q_2), .CLK(B), .K(1'b1));  // open: Q_2
  nor nor_1 (nor_1_out, ~nand_2_out, ~nand_1_out);  // NOR_Gate
  _7473__JK_flip_flop_w__clear u_7473_jk_flip_flop_w_clear_2 (
    .Q(QC), .CLR(nor_2_out), .J(1'b1), .CLK(QB), .K(1'b1));  // open: Q_2
  nor nor_2 (nor_2_out, ~nand_2_out, ~nand_1_out);  // NOR_Gate
  _7476__JK_flip_flop_w__clear___preset u_7476_jk_flip_flop_w_clear_preset_2 (
    .J(and_1_out), .CLK(B), .K(QD), .Q(QD), .Q_2(n7476_jk_flip_flop_w_clear_preset_2_q_2), .PR(nand_1_out),
    .CLR(nand_2_out));

  // Notes on the sheet:
  //   Author: Cristian Vancea
  //   Affiliation: Technical University of Cluj-Napoca
endmodule

module _7493__asynch_binary_counter (
  input  A,
  input  B,
  input  R0_1,
  input  R0_2,
  output QA,
  output QB,
  output QC,
  output QD
);

  wire nand_1_out;

  nand nand_1 (nand_1_out, R0_1, R0_2);
  _7473__JK_flip_flop_w__clear u_7473_jk_flip_flop_w_clear_1 (
    .Q(QA), .CLR(nand_1_out), .J(1'b1), .CLK(A), .K(1'b1));  // open: Q_2
  _7473__JK_flip_flop_w__clear u_7473_jk_flip_flop_w_clear_2 (
    .Q(QB), .CLR(nand_1_out), .J(1'b1), .CLK(B), .K(1'b1));  // open: Q_2
  _7473__JK_flip_flop_w__clear u_7473_jk_flip_flop_w_clear_3 (
    .Q(QC), .CLR(nand_1_out), .J(1'b1), .CLK(QB), .K(1'b1));  // open: Q_2
  _7473__JK_flip_flop_w__clear u_7473_jk_flip_flop_w_clear_4 (
    .Q(QD), .CLR(nand_1_out), .J(1'b1), .CLK(QC), .K(1'b1));  // open: Q_2

  // Notes on the sheet:
  //   Author: Cristian Vancea
  //   Affiliation: Technical University of Cluj-Napoca
endmodule

module _7495__shift_reg_w__parallel_load (
  input  A,
  input  B,
  input  C,
  input  D,
  input  SER,
  input  MODE,
  input  CK1,
  input  CK2,
  output QA,
  output QB,
  output QC,
  output QD
);

  wire and_1_out, and_2_out, multiplexer_1_out, multiplexer_2_out, multiplexer_3_out, multiplexer_4_out,
       or_1_out;

  Multiplexer #(.enable("false")) multiplexer_1 (.in0(SER), .in1(A), .out(multiplexer_1_out), .sel(MODE));
  and and_1 (and_1_out, ~MODE, ~CK1);  // AND_Gate
  or or_1 (or_1_out, and_1_out, and_2_out);
  and and_2 (and_2_out, MODE, ~CK2);  // AND_Gate
  D_Flip_Flop d_ff_1 (.clk(or_1_out), .D(multiplexer_1_out), .Q(QA));  // open: Qn, preset, en, reset
  Multiplexer #(.enable("false")) multiplexer_2 (.in0(QA), .in1(B), .out(multiplexer_2_out), .sel(MODE));
  D_Flip_Flop d_ff_2 (.clk(or_1_out), .D(multiplexer_2_out), .Q(QB));  // open: Qn, preset, en, reset
  Multiplexer #(.enable("false")) multiplexer_3 (.in0(QB), .in1(C), .out(multiplexer_3_out), .sel(MODE));
  D_Flip_Flop d_ff_3 (.clk(or_1_out), .D(multiplexer_3_out), .Q(QC));  // open: Qn, preset, en, reset
  Multiplexer #(.enable("false")) multiplexer_4 (.in0(QC), .in1(D), .out(multiplexer_4_out), .sel(MODE));
  D_Flip_Flop d_ff_4 (.clk(or_1_out), .D(multiplexer_4_out), .Q(QD));  // open: Qn, preset, en, reset

  // Notes on the sheet:
  //   Author: Cristian Vancea
  //   Affiliation: Technical University of Cluj-Napoca
endmodule
