// Logisim project lab5 ex6.circ as structural Verilog: 1 circuit, main circuit main
module main (
  input  A,
  input  B,
  input  C,
  input  D,
  output p3
);

  wire and_1_out, and_2_out, not_1_out, or_1_out;

  and and_1 (and_1_out, B, not_1_out, D);
  not not_1 (not_1_out, C);
  or or_1 (or_1_out, A, and_1_out);
  and and_2 (and_2_out, C, B);
  or or_2 (p3, or_1_out, and_2_out);
endmodule
