// Logisim project tema lab7ex9.circ as structural Verilog: 1 circuit, main circuit main
module main (
  input  A,
  input  [3:0] BCDE,
  output F
);

  Multiplexer #(.select(4), .disabled(0), .enable("false")) multiplexer_1 (
    .in0(A), .in1(A), .in2(1'b1), .in3(1'b1), .in4(A), .in5(1'b1), .in6(1'b0), .in7(1'b0), .in8(1'b1),
    .in9(1'b0), .in10(1'b1), .in11(1'b0), .in12(1'b0), .in13(1'b1), .in14(A), .in15(A), .out(F), .sel(BCDE));
endmodule
