// Logisim project lab3 a).circ as structural Verilog: 7 circuits, main circuit lab3 a
module lab3_a (
  input  a,
  input  b,
  input  c,
  output out_4
);

  wire not_1_out;

  not not_1 (not_1_out, b);
  or or_1 (out_4, a, not_1_out, c);
endmodule

module lab3_b (
  input  b,
  input  a,
  input  c,
  output out_4
);

  wire or_1_out, or_2_out;

  or or_1 (or_1_out, b, a);
  or or_2 (or_2_out, a, c);
  and and_1 (out_4, or_1_out, or_2_out);
endmodule

module lab3_c (
  input  b,
  input  c,
  input  a,
  output out_4
);

  wire and_1_out, not_1_out, not_2_out;

  and and_1 (and_1_out, b, not_1_out);
  not not_1 (not_1_out, c);
  not not_2 (not_2_out, and_1_out);
  or or_1 (out_4, not_2_out, a);
endmodule

module lab3_d (
  input  a,
  input  b,
  input  c,
  output out_4
);

  wire and_1_out, not_1_out, not_2_out, or_1_out, or_2_out;

  not not_1 (not_1_out, c);
  or or_1 (or_1_out, a, c);
  and and_1 (and_1_out, not_1_out, b);
  not not_2 (not_2_out, or_1_out);
  or or_2 (or_2_out, not_2_out, and_1_out);
  and and_2 (out_4, or_2_out, b);
endmodule

module lab3_e (
  input  a,
  input  b,
  input  c,
  output out_4
);

  wire and_1_out, and_2_out, not_1_out;

  and and_1 (and_1_out, b, c);
  not not_1 (not_1_out, and_1_out);
  and and_2 (and_2_out, a, not_1_out);
  not not_2 (out_4, and_2_out);
endmodule

module lab3_f (
  input  a,
  input  b,
  input  c,
  output out_4
);

  wire not_1_out, not_2_out, not_3_out, or_1_out, or_2_out;

  not not_1 (not_1_out, a);
  not not_2 (not_2_out, b);
  or or_1 (or_1_out, not_1_out, not_2_out);
  or or_2 (or_2_out, a, c);
  or or_3 (out_4, or_1_out, not_3_out);
  not not_3 (not_3_out, or_2_out);
endmodule

module lab3_g (
  input  a,
  input  b,
  input  c,
  output out_4
);

  wire and_1_out, and_2_out, not_1_out, not_2_out;

  not not_1 (not_1_out, c);
  and and_1 (and_1_out, a, b);
  and and_2 (and_2_out, b, not_1_out);
  not not_2 (not_2_out, and_1_out);
  or or_1 (out_4, not_2_out, and_2_out);
endmodule
