// Logisim project lab10_3.circ as structural Verilog: 1 circuit, main circuit main
module main (
  input  in_1,
  input  in_2,
  input  in_3,
  input  in_4,
  input  in_5,
  input  in_6,
  output out_7,
  output out_8,
  output out_9,
  output out_10,
  output out_11,
  output out_12
);

  wire clock_1_out;

  Clock clock_1 (.out(clock_1_out));
  _74193__up_down_binary_counter u_74193_up_down_binary_counter_1 (
    .CDn(clock_1_out), .CUp(1'b1), .BORROW(out_8), .CARRY(out_7), .QA(out_9), .QB(out_10), .QC(out_11),
    .QD(out_12), .LOAD(in_5), .CLEAR(in_6), .D(in_4), .C(in_3), .B(in_2), .A(in_1));
endmodule
