// Logisim project lab10_4.circ as structural Verilog: 1 circuit, main circuit main
module main (
  input  in_1,
  input  in_2,
  input  in_3,
  input  in_4,
  input  in_5,
  input  in_6,
  output out_7,
  output out_8,
  output out_9,
  output out_10,
  output out_11
);

  wire clock_1_out;

  Clock clock_1 (.out(clock_1_out));
  _74163__synch_binary_counter u_74163_synch_binary_counter_1 (
    .A(in_2), .B(in_3), .C(in_4), .D(in_5), .LOAD(in_1), .ENP(1'b1), .ENT(1'b1), .QA(out_8), .QB(out_9),
    .QC(out_10), .QD(out_11), .RCO(out_7), .CLK(clock_1_out), .CLEAR(in_6));
endmodule
