// Logisim project lab10_6.circ as structural Verilog: 1 circuit, main circuit main
module main (
  input  RST,
  output Q2,
  output Q0,
  output Q1,
  output Q3
);

  wire and_1_out, and_2_out, clock_1_out;

  Clock clock_1 (.out(clock_1_out));
  _7473__JK_flip_flop_w__clear u_7473_jk_flip_flop_w_clear_1 (
    .Q(Q0), .CLR(RST), .J(1'b1), .CLK(clock_1_out), .K(1'b1));  // open: Q_2
  and and_1 (and_1_out, Q0, Q1);
  _7473__JK_flip_flop_w__clear u_7473_jk_flip_flop_w_clear_2 (
    .Q(Q1), .CLR(RST), .J(Q0), .CLK(clock_1_out), .K(Q0));  // open: Q_2
  and and_2 (and_2_out, and_1_out, Q2);
  _7473__JK_flip_flop_w__clear u_7473_jk_flip_flop_w_clear_3 (
    .Q(Q2), .CLR(RST), .J(and_1_out), .CLK(clock_1_out), .K(and_1_out));  // open: Q_2
  _7473__JK_flip_flop_w__clear u_7473_jk_flip_flop_w_clear_4 (
    .Q(Q3), .CLR(RST), .J(and_2_out), .CLK(clock_1_out), .K(and_2_out));  // open: Q_2
endmodule
